// Logisim project And.circ as structural Verilog
module D_Flip_Flop (
  input  D,
  input  Clock,
  output out_3,
  output out_4
);

  wire and_1_out, and_2_out, not_1_out;

  not not_1 (not_1_out, D);
  and and_1 (and_1_out, not_1_out, Clock);
  and and_2 (and_2_out, Clock, D);
  nor nor_1 (out_3, and_1_out, out_4);
  nor nor_2 (out_4, out_3, and_2_out);
endmodule

module Register (
  input  [17:0] in_1,
  input  in_2,
  output [17:0] out_3
);

  D_Flip_Flop d_ff_1 (.D(in_1[17]), .Clock(in_2), .out_3(out_3[17]));  // open: out_4
  D_Flip_Flop d_ff_2 (.D(in_1[16]), .Clock(in_2), .out_3(out_3[16]));  // open: out_4
  D_Flip_Flop d_ff_3 (.D(in_1[15]), .Clock(in_2), .out_3(out_3[15]));  // open: out_4
  D_Flip_Flop d_ff_4 (.D(in_1[14]), .Clock(in_2), .out_3(out_3[14]));  // open: out_4
  D_Flip_Flop d_ff_5 (.D(in_1[13]), .Clock(in_2), .out_3(out_3[13]));  // open: out_4
  D_Flip_Flop d_ff_6 (.D(in_1[12]), .Clock(in_2), .out_3(out_3[12]));  // open: out_4
  D_Flip_Flop d_ff_7 (.D(in_1[11]), .Clock(in_2), .out_3(out_3[11]));  // open: out_4
  D_Flip_Flop d_ff_8 (.D(in_1[10]), .Clock(in_2), .out_3(out_3[10]));  // open: out_4
  D_Flip_Flop d_ff_9 (.D(in_1[9]), .Clock(in_2), .out_3(out_3[9]));  // open: out_4
  D_Flip_Flop d_ff_10 (.D(in_1[8]), .Clock(in_2), .out_3(out_3[8]));  // open: out_4
  D_Flip_Flop d_ff_11 (.D(in_1[7]), .Clock(in_2), .out_3(out_3[7]));  // open: out_4
  D_Flip_Flop d_ff_12 (.D(in_1[6]), .Clock(in_2), .out_3(out_3[6]));  // open: out_4
  D_Flip_Flop d_ff_13 (.D(in_1[4]), .Clock(in_2), .out_3(out_3[4]));  // open: out_4
  D_Flip_Flop d_ff_14 (.D(in_1[5]), .Clock(in_2), .out_3(out_3[5]));  // open: out_4
  D_Flip_Flop d_ff_15 (.D(in_1[3]), .Clock(in_2), .out_3(out_3[3]));  // open: out_4
  D_Flip_Flop d_ff_16 (.D(in_1[2]), .Clock(in_2), .out_3(out_3[2]));  // open: out_4
  D_Flip_Flop d_ff_17 (.D(in_1[1]), .Clock(in_2), .out_3(out_3[1]));  // open: out_4
  D_Flip_Flop d_ff_18 (.D(in_1[0]), .Clock(in_2), .out_3(out_3[0]));  // open: out_4
endmodule

module Register_File (
);

  Register register_1 ();  // open: in_1, in_2, out_3
  Register register_2 ();  // open: in_1, in_2, out_3
endmodule

module Half_Adder (
  input  in_1,
  input  in_2,
  output Cout,
  output S
);

  and and_1 (Cout, in_1, in_2);
  xor xor_1 (S, in_1, in_2);
endmodule

module Reg_Adder (
  input  [17:0] Reg_2,
  input  [17:0] immediate_Value,
  input  in_3,
  input  [17:0] Reg_1,
  output [17:0] out_5
);

  wire full_adder_1_cout, full_adder_2_cout, full_adder_3_cout, full_adder_4_cout, full_adder_5_cout,
       full_adder_6_cout, full_adder_7_cout, full_adder_8_cout, full_adder_9_cout, full_adder_10_cout,
       full_adder_12_cout, full_adder_13_cout, full_adder_14_cout, full_adder_15_cout, full_adder_16_cout,
       full_adder_17_cout, half_adder_1_cout;
  wire [17:0] multiplexer_1_out;

  Full_Adder full_adder_1 (
    .i0(Reg_1[9]), .i1(multiplexer_1_out[16]), .Cin(full_adder_3_cout), .Sum(out_5[9]),
    .Cout(full_adder_1_cout));
  Full_Adder full_adder_2 (
    .i0(Reg_1[7]), .i1(multiplexer_1_out[7]), .Cin(full_adder_5_cout), .Sum(out_5[7]),
    .Cout(full_adder_2_cout));
  Full_Adder full_adder_3 (
    .i0(Reg_1[8]), .i1(multiplexer_1_out[17]), .Cin(full_adder_2_cout), .Sum(out_5[8]),
    .Cout(full_adder_3_cout));
  Full_Adder full_adder_4 (
    .i0(Reg_1[5]), .i1(multiplexer_1_out[5]), .Cin(full_adder_7_cout), .Sum(out_5[5]),
    .Cout(full_adder_4_cout));
  Full_Adder full_adder_5 (
    .i0(Reg_1[6]), .i1(multiplexer_1_out[6]), .Cin(full_adder_4_cout), .Sum(out_5[6]),
    .Cout(full_adder_5_cout));
  Full_Adder full_adder_6 (
    .i0(Reg_1[3]), .i1(multiplexer_1_out[3]), .Cin(full_adder_9_cout), .Sum(out_5[3]),
    .Cout(full_adder_6_cout));
  Full_Adder full_adder_7 (
    .i0(Reg_1[4]), .i1(multiplexer_1_out[4]), .Cin(full_adder_6_cout), .Sum(out_5[4]),
    .Cout(full_adder_7_cout));
  Full_Adder full_adder_8 (
    .i0(Reg_1[1]), .i1(multiplexer_1_out[1]), .Cin(half_adder_1_cout), .Sum(out_5[1]),
    .Cout(full_adder_8_cout));
  Full_Adder full_adder_9 (
    .i0(Reg_1[2]), .i1(multiplexer_1_out[2]), .Cin(full_adder_8_cout), .Sum(out_5[2]),
    .Cout(full_adder_9_cout));
  Half_Adder half_adder_1 (.in_1(Reg_1[0]), .in_2(multiplexer_1_out[0]), .Cout(half_adder_1_cout), .S(out_5[0]));
  Multiplexer #(.width(18), .enable("false")) multiplexer_1 (
    .in0(Reg_2), .in1(immediate_Value),
    .out({multiplexer_1_out[17:10], multiplexer_1_out[16], multiplexer_1_out[17], multiplexer_1_out[7:0]}),
    .sel(in_3));
  Full_Adder full_adder_10 (
    .i0(Reg_1[16]), .i1(multiplexer_1_out[16]), .Cin(full_adder_13_cout), .Sum(out_5[16]),
    .Cout(full_adder_10_cout));
  Full_Adder full_adder_11 (
    .i0(Reg_1[17]), .i1(multiplexer_1_out[17]), .Cin(full_adder_10_cout), .Sum(out_5[17]));  // open: Cout
  Full_Adder full_adder_12 (
    .i0(Reg_1[14]), .i1(multiplexer_1_out[14]), .Cin(full_adder_15_cout), .Sum(out_5[14]),
    .Cout(full_adder_12_cout));
  Full_Adder full_adder_13 (
    .i0(Reg_1[15]), .i1(multiplexer_1_out[15]), .Cin(full_adder_12_cout), .Sum(out_5[15]),
    .Cout(full_adder_13_cout));
  Full_Adder full_adder_14 (
    .i0(Reg_1[12]), .i1(multiplexer_1_out[12]), .Cin(full_adder_17_cout), .Sum(out_5[12]),
    .Cout(full_adder_14_cout));
  Full_Adder full_adder_15 (
    .i0(Reg_1[13]), .i1(multiplexer_1_out[13]), .Cin(full_adder_14_cout), .Sum(out_5[13]),
    .Cout(full_adder_15_cout));
  Full_Adder full_adder_16 (
    .i0(Reg_1[10]), .i1(multiplexer_1_out[10]), .Cin(full_adder_1_cout), .Sum(out_5[10]),
    .Cout(full_adder_16_cout));
  Full_Adder full_adder_17 (
    .i0(Reg_1[11]), .i1(multiplexer_1_out[11]), .Cin(full_adder_16_cout), .Sum(out_5[11]),
    .Cout(full_adder_17_cout));
endmodule

module Full_Adder (
  input  i0,
  input  i1,
  input  Cin,
  output Sum,
  output Cout
);

  wire and_1_out, and_2_out, xor_1_out;

  xor xor_1 (xor_1_out, i0, i1);
  xor xor_2 (Sum, xor_1_out, Cin);
  and and_1 (and_1_out, xor_1_out, Cin);
  or or_1 (Cout, and_1_out, and_2_out);
  and and_2 (and_2_out, i0, i1);
endmodule
