// Logisim project CPU.circ as structural Verilog: 27 circuits, main circuit main
module main (
  input  [9:0] in_1,
  input  [9:0] in_2,
  input  in_3,
  input  in_4,
  input  [17:0] in_5,
  output [17:0] out_6
);

  wire _3_reg, ADD, ADDI, ALU_Signal, AND, ANDI, CMP, IMM_Signal, JA, JAE, JB, JBE, JE, JUMP, LD, MemLoad,
       MemStore, NAND, NOR, ST, WE_to_RegFile;
  wire [1:0] Aluselector;
  wire [3:0] Dest_1, Opcode, RegLoaded, Src1, Src2;
  wire [9:0] jump_unit_1_out_6, LoadAddress, multiplexer_1_out;
  wire [12:0] JumpImm;
  wire [13:0] control_unit_1_fullcode;
  wire [17:0] alu_arithmetic_logic_unit_1_output, multiplexer_2_out, multiplexer_5_out, srcData_1, srcData_2;
  wire [17:13] multiplexer_3_out;
  wire [17:14] multiplexer_4_out;

  Decoder #(.select(4), .enable("false")) decoder_1 (
    .out0(ADD), .out1(AND), .out2(NAND), .out3(NOR), .out4(ADDI), .out5(ANDI), .out6(LD), .out7(ST),
    .out8(CMP), .out9(JUMP), .out10(JA), .out11(JE), .out12(JB), .out13(JAE), .out14(JBE), .sel(Opcode));  // open: out15
  Multiplexer #(.width(10), .enable("false")) multiplexer_1 (
    .in0(in_1), .in1(jump_unit_1_out_6), .out(multiplexer_1_out), .sel(JUMP));
  Memory_Unit memory_unit_1 (.PC(multiplexer_1_out), .mx_controller(in_3), .counter(in_4), .out_4(out_6));
  Control_Unit control_unit_1 (
    .in_1(in_2), .in_2(in_3), .in_3(in_4), .FullCode({Opcode, control_unit_1_fullcode}),
    .RegFileWrite(WE_to_RegFile), ._3_Reg_signal(_3_reg), .Jump(JUMP), .MemoryStore(MemStore),
    .MemoryLoad(MemLoad), .ALU_signal(ALU_Signal), .imm_signal(IMM_Signal));
  Multiplexer #(.width(18), .enable("false")) multiplexer_2 (
    .in1(out_6), .out({multiplexer_2_out[17:16], Aluselector, Dest_1, Src1, Src2, multiplexer_2_out[1:0]}),
    .sel(ALU_Signal));  // open: in0
  JUMP_Unit jump_unit_1 (
    .immediate(JumpImm), .PC(in_1), .in_4(in_3), .in_5(in_4), .Enable(JUMP), .out_6(jump_unit_1_out_6));
  Multiplexer #(.width(18), .enable("false")) multiplexer_3 (
    .in1(out_6), .out({multiplexer_3_out, JumpImm}), .sel(JUMP));  // open: in0
  Multiplexer #(.width(18), .enable("false")) multiplexer_4 (
    .in1(out_6), .out({multiplexer_4_out, RegLoaded, LoadAddress}), .sel(MemLoad));  // open: in0
  load load_1 (.\reg (RegLoaded), .address(LoadAddress), .Load_Enable(MemLoad));
  ALU__Arithmetic_Logic_Unit alu_arithmetic_logic_unit_1 (
    .Input2(srcData_2), .in_4(IMM_Signal), .Input1(srcData_1), .Select(Aluselector),
    .Output(alu_arithmetic_logic_unit_1_output));
  Register_File register_file_1 (
    .Src_Data_1(srcData_1), .Src_Data_2(srcData_2), .Dest_Reg(Dest_1), .write_enable(ALU_Signal),
    .write_data(multiplexer_5_out), .Src_Reg_1(Src1), .Src_Reg_2(Src2), .clk(1'b1));
  Multiplexer #(.width(18), .enable("false")) multiplexer_5 (
    .in0(alu_arithmetic_logic_unit_1_output), .in1(in_5), .out(multiplexer_5_out), .sel(IMM_Signal));
endmodule

module D_Flip_Flop (
  input  D,
  input  Clock,
  output out_3,
  output out_4
);

  wire and_1_out, and_2_out, not_1_out;

  not not_1 (not_1_out, D);
  and and_1 (and_1_out, not_1_out, Clock);
  and and_2 (and_2_out, Clock, D);
  nor nor_1 (out_3, and_1_out, out_4);
  nor nor_2 (out_4, out_3, and_2_out);
endmodule

module _18_bit_Register (
  input  [17:0] in_1,
  input  Load,
  input  in_3,
  output [17:0] out_4
);

  wire multiplexer_1_out, multiplexer_2_out, multiplexer_3_out, multiplexer_4_out, multiplexer_5_out,
       multiplexer_6_out, multiplexer_7_out, multiplexer_8_out, multiplexer_9_out, multiplexer_10_out,
       multiplexer_11_out, multiplexer_12_out, multiplexer_13_out, multiplexer_14_out, multiplexer_15_out,
       multiplexer_16_out, multiplexer_17_out, multiplexer_18_out;
  wire [17:0] d_ff_18_out_3;

  Multiplexer #(.enable("false")) multiplexer_1 (
    .in0(d_ff_18_out_3[17]), .in1(in_1[17]), .out(multiplexer_1_out), .sel(Load));
  Multiplexer #(.enable("false")) multiplexer_2 (
    .in0(d_ff_18_out_3[16]), .in1(in_1[16]), .out(multiplexer_2_out), .sel(Load));
  D_Flip_Flop d_ff_1 (.D(multiplexer_1_out), .Clock(in_3), .out_3(d_ff_18_out_3[17]));  // open: out_4
  Multiplexer #(.enable("false")) multiplexer_3 (
    .in0(d_ff_18_out_3[15]), .in1(in_1[15]), .out(multiplexer_3_out), .sel(Load));
  D_Flip_Flop d_ff_2 (.D(multiplexer_2_out), .Clock(in_3), .out_3(d_ff_18_out_3[16]));  // open: out_4
  D_Flip_Flop d_ff_3 (.D(multiplexer_3_out), .Clock(in_3), .out_3(d_ff_18_out_3[15]));  // open: out_4
  Multiplexer #(.enable("false")) multiplexer_4 (
    .in0(d_ff_18_out_3[13]), .in1(in_1[13]), .out(multiplexer_4_out), .sel(Load));
  Multiplexer #(.enable("false")) multiplexer_5 (
    .in0(d_ff_18_out_3[14]), .in1(in_1[14]), .out(multiplexer_5_out), .sel(Load));
  D_Flip_Flop d_ff_4 (.D(multiplexer_5_out), .Clock(in_3), .out_3(d_ff_18_out_3[14]));  // open: out_4
  Multiplexer #(.enable("false")) multiplexer_6 (
    .in0(d_ff_18_out_3[12]), .in1(in_1[12]), .out(multiplexer_6_out), .sel(Load));
  D_Flip_Flop d_ff_5 (.D(multiplexer_4_out), .Clock(in_3), .out_3(d_ff_18_out_3[13]));  // open: out_4
  Multiplexer #(.enable("false")) multiplexer_7 (
    .in0(d_ff_18_out_3[11]), .in1(in_1[11]), .out(multiplexer_7_out), .sel(Load));
  D_Flip_Flop d_ff_6 (.D(multiplexer_7_out), .Clock(in_3), .out_3(d_ff_18_out_3[11]));  // open: out_4
  D_Flip_Flop d_ff_7 (.D(multiplexer_6_out), .Clock(in_3), .out_3(d_ff_18_out_3[12]));  // open: out_4
  Multiplexer #(.enable("false")) multiplexer_8 (
    .in0(d_ff_18_out_3[9]), .in1(in_1[9]), .out(multiplexer_8_out), .sel(Load));
  Multiplexer #(.enable("false")) multiplexer_9 (
    .in0(d_ff_18_out_3[10]), .in1(in_1[10]), .out(multiplexer_9_out), .sel(Load));
  D_Flip_Flop d_ff_8 (.D(multiplexer_9_out), .Clock(in_3), .out_3(d_ff_18_out_3[10]));  // open: out_4
  Multiplexer #(.enable("false")) multiplexer_10 (
    .in0(d_ff_18_out_3[8]), .in1(in_1[8]), .out(multiplexer_10_out), .sel(Load));
  D_Flip_Flop d_ff_9 (.D(multiplexer_8_out), .Clock(in_3), .out_3(d_ff_18_out_3[9]));  // open: out_4
  Multiplexer #(.enable("false")) multiplexer_11 (
    .in0(d_ff_18_out_3[7]), .in1(in_1[7]), .out(multiplexer_11_out), .sel(Load));
  D_Flip_Flop d_ff_10 (.D(multiplexer_10_out), .Clock(in_3), .out_3(d_ff_18_out_3[8]));  // open: out_4
  D_Flip_Flop d_ff_11 (.D(multiplexer_11_out), .Clock(in_3), .out_3(d_ff_18_out_3[7]));  // open: out_4
  Multiplexer #(.enable("false")) multiplexer_12 (
    .in0(d_ff_18_out_3[5]), .in1(in_1[5]), .out(multiplexer_12_out), .sel(Load));
  Multiplexer #(.enable("false")) multiplexer_13 (
    .in0(d_ff_18_out_3[6]), .in1(in_1[6]), .out(multiplexer_13_out), .sel(Load));
  D_Flip_Flop d_ff_12 (.D(multiplexer_13_out), .Clock(in_3), .out_3(d_ff_18_out_3[6]));  // open: out_4
  Multiplexer #(.enable("false")) multiplexer_14 (
    .in0(d_ff_18_out_3[4]), .in1(in_1[4]), .out(multiplexer_14_out), .sel(Load));
  D_Flip_Flop d_ff_13 (.D(multiplexer_12_out), .Clock(in_3), .out_3(d_ff_18_out_3[5]));  // open: out_4
  Multiplexer #(.enable("false")) multiplexer_15 (
    .in0(d_ff_18_out_3[3]), .in1(in_1[3]), .out(multiplexer_15_out), .sel(Load));
  D_Flip_Flop d_ff_14 (.D(multiplexer_14_out), .Clock(in_3), .out_3(d_ff_18_out_3[4]));  // open: out_4
  D_Flip_Flop d_ff_15 (.D(multiplexer_15_out), .Clock(in_3), .out_3(d_ff_18_out_3[3]));  // open: out_4
  Multiplexer #(.enable("false")) multiplexer_16 (
    .in0(d_ff_18_out_3[2]), .in1(in_1[2]), .out(multiplexer_16_out), .sel(Load));
  Multiplexer #(.enable("false")) multiplexer_17 (
    .in0(d_ff_18_out_3[1]), .in1(in_1[1]), .out(multiplexer_17_out), .sel(Load));
  D_Flip_Flop d_ff_16 (.D(multiplexer_16_out), .Clock(in_3), .out_3(d_ff_18_out_3[2]));  // open: out_4
  Multiplexer #(.enable("false")) multiplexer_18 (
    .in0(d_ff_18_out_3[0]), .in1(in_1[0]), .out(multiplexer_18_out), .sel(Load));
  D_Flip_Flop d_ff_17 (.D(multiplexer_17_out), .Clock(in_3), .out_3(d_ff_18_out_3[1]));  // open: out_4
  D_Flip_Flop d_ff_18 (.D(multiplexer_18_out), .Clock(in_3), .out_3(d_ff_18_out_3[0]));  // open: out_4
  Multiplexer #(.width(18), .enable("false")) multiplexer_19 (
    .in0({18{1'b0}}), .in1(d_ff_18_out_3), .out(out_4), .sel(Load));
endmodule

// ALU
module ALU__Arithmetic_Logic_Unit (
  input  [17:0] Input1,
  input  [1:0] Select,
  input  [17:0] Input2,
  input  in_4,
  output [17:0] Output
);

  wire [17:0] addgate_1_out_5, andgate_1_out_5, nandgate_1_out_3, norgate_1_out_3;

  addGate addgate_1 (
    .regData1(Input1), .regData2(Input2), ._16th_bit(in_4), .out_5(addgate_1_out_5));  // open: immValue
  andGate andgate_1 (
    .regData1(Input1), .regData2(Input2), ._16th_bit(in_4), .out_5(andgate_1_out_5));  // open: immValue
  nandGate nandgate_1 (.regData1(Input1), .regData2(Input2), .out_3(nandgate_1_out_3));
  norGate norgate_1 (.regData1(Input1), .regData2(Input2), .out_3(norgate_1_out_3));
  Multiplexer #(.select(2), .width(18), .enable("false")) multiplexer_1 (
    .in0(addgate_1_out_5), .in1(andgate_1_out_5), .in2(nandgate_1_out_3), .in3(norgate_1_out_3),
    .out(Output), .sel(Select));
  // Probe on Output
endmodule

module Half_Adder (
  input  in_1,
  input  in_2,
  output Cout,
  output S
);

  and and_1 (Cout, in_1, in_2);
  xor xor_1 (S, in_1, in_2);
endmodule

module _18_bit_Adder (
  input  [17:0] Reg_2,
  input  [17:0] Reg_1,
  output [17:0] out_3
);

  wire full_adder_1_cout, full_adder_2_cout, full_adder_3_cout, full_adder_4_cout, full_adder_5_cout,
       full_adder_6_cout, full_adder_7_cout, full_adder_8_cout, full_adder_9_cout, full_adder_10_cout,
       full_adder_12_cout, full_adder_13_cout, full_adder_14_cout, full_adder_15_cout, full_adder_16_cout,
       full_adder_17_cout, half_adder_1_cout;

  Full_Adder full_adder_1 (
    .i0(Reg_1[9]), .i1(Reg_2[9]), .Cin(full_adder_3_cout), .Sum(out_3[9]), .Cout(full_adder_1_cout));
  Full_Adder full_adder_2 (
    .i0(Reg_1[7]), .i1(Reg_2[7]), .Cin(full_adder_5_cout), .Sum(out_3[7]), .Cout(full_adder_2_cout));
  Full_Adder full_adder_3 (
    .i0(Reg_1[8]), .i1(Reg_2[8]), .Cin(full_adder_2_cout), .Sum(out_3[8]), .Cout(full_adder_3_cout));
  Full_Adder full_adder_4 (
    .i0(Reg_1[5]), .i1(Reg_2[5]), .Cin(full_adder_7_cout), .Sum(out_3[5]), .Cout(full_adder_4_cout));
  Full_Adder full_adder_5 (
    .i0(Reg_1[6]), .i1(Reg_2[6]), .Cin(full_adder_4_cout), .Sum(out_3[6]), .Cout(full_adder_5_cout));
  Full_Adder full_adder_6 (
    .i0(Reg_1[3]), .i1(Reg_2[3]), .Cin(full_adder_9_cout), .Sum(out_3[3]), .Cout(full_adder_6_cout));
  Full_Adder full_adder_7 (
    .i0(Reg_1[4]), .i1(Reg_2[4]), .Cin(full_adder_6_cout), .Sum(out_3[4]), .Cout(full_adder_7_cout));
  Full_Adder full_adder_8 (
    .i0(Reg_1[1]), .i1(Reg_2[1]), .Cin(half_adder_1_cout), .Sum(out_3[1]), .Cout(full_adder_8_cout));
  Full_Adder full_adder_9 (
    .i0(Reg_1[2]), .i1(Reg_2[2]), .Cin(full_adder_8_cout), .Sum(out_3[2]), .Cout(full_adder_9_cout));
  Half_Adder half_adder_1 (.in_1(Reg_1[0]), .in_2(Reg_2[0]), .Cout(half_adder_1_cout), .S(out_3[0]));
  Full_Adder full_adder_10 (
    .i0(Reg_1[16]), .i1(Reg_2[16]), .Cin(full_adder_13_cout), .Sum(out_3[16]), .Cout(full_adder_10_cout));
  Full_Adder full_adder_11 (.i0(Reg_1[17]), .i1(Reg_2[17]), .Cin(full_adder_10_cout), .Sum(out_3[17]));  // open: Cout
  Full_Adder full_adder_12 (
    .i0(Reg_1[14]), .i1(Reg_2[14]), .Cin(full_adder_15_cout), .Sum(out_3[14]), .Cout(full_adder_12_cout));
  Full_Adder full_adder_13 (
    .i0(Reg_1[15]), .i1(Reg_2[15]), .Cin(full_adder_12_cout), .Sum(out_3[15]), .Cout(full_adder_13_cout));
  Full_Adder full_adder_14 (
    .i0(Reg_1[12]), .i1(Reg_2[12]), .Cin(full_adder_17_cout), .Sum(out_3[12]), .Cout(full_adder_14_cout));
  Full_Adder full_adder_15 (
    .i0(Reg_1[13]), .i1(Reg_2[13]), .Cin(full_adder_14_cout), .Sum(out_3[13]), .Cout(full_adder_15_cout));
  Full_Adder full_adder_16 (
    .i0(Reg_1[10]), .i1(Reg_2[10]), .Cin(full_adder_1_cout), .Sum(out_3[10]), .Cout(full_adder_16_cout));
  Full_Adder full_adder_17 (
    .i0(Reg_1[11]), .i1(Reg_2[11]), .Cin(full_adder_16_cout), .Sum(out_3[11]), .Cout(full_adder_17_cout));
endmodule

module Full_Adder (
  input  i0,
  input  i1,
  input  Cin,
  output Sum,
  output Cout
);

  wire and_1_out, and_2_out, xor_1_out;

  xor xor_1 (xor_1_out, i0, i1);
  xor xor_2 (Sum, xor_1_out, Cin);
  and and_1 (and_1_out, xor_1_out, Cin);
  or or_1 (Cout, and_1_out, and_2_out);
  and and_2 (and_2_out, i0, i1);
endmodule

module Memory_File (
  input  [9:0] in_1,
  output [17:0] out_2,
  output [3:0] OPCODE,
  output [3:0] DEST_REG,
  output [3:0] SRC_REG_1,
  output [3:0] SRC_REG_2
);

  wire [9:0] PC_p4;
  wire [17:16] ram_1_data;

  // _10_bit_Register PC: pin names not known; wires that end beside it: in_1, 1'b0, 1'b1, PC_p4
  RAM #(.addrWidth(10), .dataWidth(18)) ram_1 (
    .addr(PC_p4), .data({ram_1_data, SRC_REG_2, SRC_REG_1, DEST_REG, OPCODE}));  // open: sel, clk, ld, clr
endmodule

module JUMP_Unit (
  input  [12:0] immediate,
  input  Enable,
  input  [9:0] PC,
  input  in_4,
  input  in_5,
  output [9:0] out_6
);

  wire [9:0] bit_extender_1_out, n10_bit_adder_1_out_3, program_counter_pc_1_out_4;

  Bit_Extender #(.in_width(13), .out_width(10)) bit_extender_1 (.in(immediate), .out(bit_extender_1_out));
  Program_Counter_PC program_counter_pc_1 (
    .in_1(PC), .First_pin(in_4), .stopper(in_5), .out_4(program_counter_pc_1_out_4));
  _10_bit_adder u_10_bit_adder_1 (
    .out_3(n10_bit_adder_1_out_3), .PC_2(program_counter_pc_1_out_4), .PC(bit_extender_1_out));
  assign out_6 = Enable ? n10_bit_adder_1_out_3 : 10'bz;  // Controlled_Buffer controlled_buffer_1
endmodule

module CMP_Unit (
  input  [17:0] in_1,
  input  [17:0] in_2,
  output eq,
  output gt,
  output lt
);

  wire full_cmp_1_eq_2, full_cmp_1_g, full_cmp_1_lt_2, full_cmp_2_eq_2, full_cmp_2_g, full_cmp_2_lt_2,
       full_cmp_3_eq_2, full_cmp_3_g, full_cmp_3_lt_2, full_cmp_4_eq_2, full_cmp_4_g, full_cmp_4_lt_2,
       full_cmp_5_eq_2, full_cmp_5_g, full_cmp_5_lt_2, full_cmp_6_eq_2, full_cmp_6_g, full_cmp_6_lt_2,
       full_cmp_7_eq_2, full_cmp_7_g, full_cmp_7_lt_2, full_cmp_8_eq_2, full_cmp_8_g, full_cmp_8_lt_2,
       full_cmp_9_eq_2, full_cmp_9_g, full_cmp_9_lt_2, full_cmp_10_eq_2, full_cmp_10_g, full_cmp_10_lt_2,
       full_cmp_11_eq_2, full_cmp_11_g, full_cmp_11_lt_2, full_cmp_12_eq_2, full_cmp_12_g, full_cmp_12_lt_2,
       full_cmp_13_eq_2, full_cmp_13_g, full_cmp_13_lt_2, full_cmp_14_eq_2, full_cmp_14_g, full_cmp_14_lt_2,
       full_cmp_15_eq_2, full_cmp_15_g, full_cmp_15_lt_2, full_cmp_16_eq_2, full_cmp_16_g, full_cmp_16_lt_2,
       half_cmp_1_eq, half_cmp_1_gt, half_cmp_1_lt;

  half_cmp half_cmp_1 (.a(in_1[17]), .b(in_2[17]), .eq(half_cmp_1_eq), .gt(half_cmp_1_gt), .lt(half_cmp_1_lt));
  full_cmp full_cmp_1 (
    .a(in_1[16]), .b(in_2[16]), .gt(half_cmp_1_gt), .lt(half_cmp_1_lt), .eq(half_cmp_1_eq), .g(full_cmp_1_g),
    .lt_2(full_cmp_1_lt_2), .eq_2(full_cmp_1_eq_2));
  full_cmp full_cmp_2 (
    .a(in_1[15]), .b(in_2[15]), .gt(full_cmp_1_g), .lt(full_cmp_1_lt_2), .eq(full_cmp_1_eq_2),
    .g(full_cmp_2_g), .lt_2(full_cmp_2_lt_2), .eq_2(full_cmp_2_eq_2));
  full_cmp full_cmp_3 (
    .a(in_1[14]), .b(in_2[14]), .gt(full_cmp_2_g), .lt(full_cmp_2_lt_2), .eq(full_cmp_2_eq_2),
    .g(full_cmp_3_g), .lt_2(full_cmp_3_lt_2), .eq_2(full_cmp_3_eq_2));
  full_cmp full_cmp_4 (
    .a(in_1[13]), .b(in_2[13]), .gt(full_cmp_3_g), .lt(full_cmp_3_lt_2), .eq(full_cmp_3_eq_2),
    .g(full_cmp_4_g), .lt_2(full_cmp_4_lt_2), .eq_2(full_cmp_4_eq_2));
  full_cmp full_cmp_5 (
    .a(in_1[12]), .b(in_2[12]), .gt(full_cmp_4_g), .lt(full_cmp_4_lt_2), .eq(full_cmp_4_eq_2),
    .g(full_cmp_5_g), .lt_2(full_cmp_5_lt_2), .eq_2(full_cmp_5_eq_2));
  full_cmp full_cmp_6 (
    .a(in_1[11]), .b(in_2[11]), .gt(full_cmp_5_g), .lt(full_cmp_5_lt_2), .eq(full_cmp_5_eq_2),
    .g(full_cmp_6_g), .lt_2(full_cmp_6_lt_2), .eq_2(full_cmp_6_eq_2));
  full_cmp full_cmp_7 (
    .a(in_1[10]), .b(in_2[10]), .gt(full_cmp_6_g), .lt(full_cmp_6_lt_2), .eq(full_cmp_6_eq_2),
    .g(full_cmp_7_g), .lt_2(full_cmp_7_lt_2), .eq_2(full_cmp_7_eq_2));
  full_cmp full_cmp_8 (
    .a(in_1[8]), .b(in_2[8]), .gt(full_cmp_9_g), .lt(full_cmp_9_lt_2), .eq(full_cmp_9_eq_2),
    .g(full_cmp_8_g), .lt_2(full_cmp_8_lt_2), .eq_2(full_cmp_8_eq_2));
  full_cmp full_cmp_9 (
    .a(in_1[9]), .b(in_2[9]), .gt(full_cmp_7_g), .lt(full_cmp_7_lt_2), .eq(full_cmp_7_eq_2),
    .g(full_cmp_9_g), .lt_2(full_cmp_9_lt_2), .eq_2(full_cmp_9_eq_2));
  full_cmp full_cmp_10 (
    .a(in_1[7]), .b(in_2[7]), .gt(full_cmp_8_g), .lt(full_cmp_8_lt_2), .eq(full_cmp_8_eq_2),
    .g(full_cmp_10_g), .lt_2(full_cmp_10_lt_2), .eq_2(full_cmp_10_eq_2));
  full_cmp full_cmp_11 (
    .a(in_1[6]), .b(in_2[6]), .gt(full_cmp_10_g), .lt(full_cmp_10_lt_2), .eq(full_cmp_10_eq_2),
    .g(full_cmp_11_g), .lt_2(full_cmp_11_lt_2), .eq_2(full_cmp_11_eq_2));
  full_cmp full_cmp_12 (
    .a(in_1[4]), .b(in_2[4]), .gt(full_cmp_13_g), .lt(full_cmp_13_lt_2), .eq(full_cmp_13_eq_2),
    .g(full_cmp_12_g), .lt_2(full_cmp_12_lt_2), .eq_2(full_cmp_12_eq_2));
  full_cmp full_cmp_13 (
    .a(in_1[5]), .b(in_2[5]), .gt(full_cmp_11_g), .lt(full_cmp_11_lt_2), .eq(full_cmp_11_eq_2),
    .g(full_cmp_13_g), .lt_2(full_cmp_13_lt_2), .eq_2(full_cmp_13_eq_2));
  full_cmp full_cmp_14 (
    .a(in_1[3]), .b(in_2[3]), .gt(full_cmp_12_g), .lt(full_cmp_12_lt_2), .eq(full_cmp_12_eq_2),
    .g(full_cmp_14_g), .lt_2(full_cmp_14_lt_2), .eq_2(full_cmp_14_eq_2));
  full_cmp full_cmp_15 (
    .a(in_1[2]), .b(in_2[2]), .gt(full_cmp_14_g), .lt(full_cmp_14_lt_2), .eq(full_cmp_14_eq_2),
    .g(full_cmp_15_g), .lt_2(full_cmp_15_lt_2), .eq_2(full_cmp_15_eq_2));
  full_cmp full_cmp_16 (
    .a(in_1[1]), .b(in_2[1]), .gt(full_cmp_15_g), .lt(full_cmp_15_lt_2), .eq(full_cmp_15_eq_2),
    .g(full_cmp_16_g), .lt_2(full_cmp_16_lt_2), .eq_2(full_cmp_16_eq_2));
  full_cmp full_cmp_17 (
    .a(in_1[0]), .b(in_2[0]), .gt(full_cmp_16_g), .lt(full_cmp_16_lt_2), .eq(full_cmp_16_eq_2), .g(gt),
    .lt_2(lt), .eq_2(eq));
endmodule

module _10_bit_Register (
  input  [9:0] in_1,
  input  Load,
  output [9:0] out_3
);

  wire multiplexer_1_out, multiplexer_2_out, multiplexer_3_out, multiplexer_4_out, multiplexer_5_out,
       multiplexer_6_out, multiplexer_7_out, multiplexer_8_out, multiplexer_9_out, multiplexer_10_out;

  Multiplexer #(.enable("false")) multiplexer_1 (.in0(out_3[9]), .in1(in_1[9]), .out(multiplexer_1_out), .sel(Load));
  Multiplexer #(.enable("false")) multiplexer_2 (.in0(out_3[8]), .in1(in_1[8]), .out(multiplexer_2_out), .sel(Load));
  D_Flip_Flop d_ff_1 (.D(multiplexer_1_out), .Clock(1'b1), .out_3(out_3[9]));  // open: out_4
  Multiplexer #(.enable("false")) multiplexer_3 (.in0(out_3[7]), .in1(in_1[7]), .out(multiplexer_3_out), .sel(Load));
  D_Flip_Flop d_ff_2 (.D(multiplexer_3_out), .Clock(1'b1), .out_3(out_3[7]));  // open: out_4
  D_Flip_Flop d_ff_3 (.D(multiplexer_2_out), .Clock(1'b1), .out_3(out_3[8]));  // open: out_4
  Multiplexer #(.enable("false")) multiplexer_4 (.in0(out_3[6]), .in1(in_1[6]), .out(multiplexer_4_out), .sel(Load));
  Multiplexer #(.enable("false")) multiplexer_5 (.in0(out_3[5]), .in1(in_1[5]), .out(multiplexer_5_out), .sel(Load));
  D_Flip_Flop d_ff_4 (.D(multiplexer_4_out), .Clock(1'b1), .out_3(out_3[6]));  // open: out_4
  Multiplexer #(.enable("false")) multiplexer_6 (.in0(out_3[4]), .in1(in_1[4]), .out(multiplexer_6_out), .sel(Load));
  D_Flip_Flop d_ff_5 (.D(multiplexer_5_out), .Clock(1'b1), .out_3(out_3[5]));  // open: out_4
  Multiplexer #(.enable("false")) multiplexer_7 (.in0(out_3[3]), .in1(in_1[3]), .out(multiplexer_7_out), .sel(Load));
  D_Flip_Flop d_ff_6 (.D(multiplexer_7_out), .Clock(1'b1), .out_3(out_3[3]));  // open: out_4
  D_Flip_Flop d_ff_7 (.D(multiplexer_6_out), .Clock(1'b1), .out_3(out_3[4]));  // open: out_4
  Multiplexer #(.enable("false")) multiplexer_8 (.in0(out_3[1]), .in1(in_1[1]), .out(multiplexer_8_out), .sel(Load));
  Multiplexer #(.enable("false")) multiplexer_9 (.in0(out_3[2]), .in1(in_1[2]), .out(multiplexer_9_out), .sel(Load));
  D_Flip_Flop d_ff_8 (.D(multiplexer_9_out), .Clock(1'b1), .out_3(out_3[2]));  // open: out_4
  Multiplexer #(.enable("false")) multiplexer_10 (.in0(out_3[0]), .in1(in_1[0]), .out(multiplexer_10_out), .sel(Load));
  D_Flip_Flop d_ff_9 (.D(multiplexer_8_out), .Clock(1'b1), .out_3(out_3[1]));  // open: out_4
  D_Flip_Flop d_ff_10 (.D(multiplexer_10_out), .Clock(1'b1), .out_3(out_3[0]));  // open: out_4
endmodule

module Register_File (
  input  [3:0] Dest_Reg,
  input  [3:0] Src_Reg_1,
  input  write_enable,
  input  [17:0] write_data,
  input  clk,
  input  [3:0] Src_Reg_2,
  output [17:0] Src_Data_1,
  output [17:0] Src_Data_2
);

  wire and_1_out, and_2_out, and_3_out, and_4_out, and_5_out, and_6_out, and_7_out, and_8_out, and_9_out,
       and_10_out, and_11_out, and_12_out, and_13_out, and_14_out, and_15_out, and_16_out, decoder_1_out0,
       decoder_1_out1, decoder_1_out2, decoder_1_out3, decoder_1_out4, decoder_1_out5, decoder_1_out6,
       decoder_1_out7, decoder_1_out8, decoder_1_out9, decoder_1_out10, decoder_1_out11, decoder_1_out12,
       decoder_1_out13, decoder_1_out14, decoder_1_out15;
  wire [17:0] R0_out_4, R1_out_4, R2_out_4, R3_p5, R4_p4, R5_p4, R6_p4, R7_p4, R8_p4, R9_p4, R10_p4, R11_p4,
       R12_p4, R13_p4, R14_p4, R15_p5;

  Decoder #(.select(4), .enable("false")) decoder_1 (
    .out0(decoder_1_out0), .out1(decoder_1_out1), .out2(decoder_1_out2), .out3(decoder_1_out3),
    .out4(decoder_1_out4), .out5(decoder_1_out5), .out6(decoder_1_out6), .out7(decoder_1_out7),
    .out8(decoder_1_out8), .out9(decoder_1_out9), .out10(decoder_1_out10), .out11(decoder_1_out11),
    .out12(decoder_1_out12), .out13(decoder_1_out13), .out14(decoder_1_out14), .out15(decoder_1_out15),
    .sel(Dest_Reg));
  and and_1 (and_1_out, decoder_1_out0, write_enable);
  and and_2 (and_2_out, decoder_1_out1, write_enable);
  and and_3 (and_3_out, decoder_1_out2, write_enable);
  and and_4 (and_4_out, decoder_1_out3, write_enable);
  and and_5 (and_5_out, decoder_1_out4, write_enable);
  and and_6 (and_6_out, decoder_1_out5, write_enable);
  and and_7 (and_7_out, decoder_1_out6, write_enable);
  and and_8 (and_8_out, decoder_1_out7, write_enable);
  and and_9 (and_9_out, decoder_1_out8, write_enable);
  and and_10 (and_10_out, decoder_1_out9, write_enable);
  and and_11 (and_11_out, decoder_1_out10, write_enable);
  and and_12 (and_12_out, decoder_1_out11, write_enable);
  and and_13 (and_13_out, decoder_1_out12, write_enable);
  and and_14 (and_14_out, decoder_1_out13, write_enable);
  and and_15 (and_15_out, decoder_1_out14, write_enable);
  and and_16 (and_16_out, decoder_1_out15, write_enable);
  _18_bit_Register R0 (.in_1(write_data), .Load(clk), .out_4(R0_out_4), .in_3(and_1_out));
  _18_bit_Register R1 (.in_1(write_data), .Load(clk), .out_4(R1_out_4), .in_3(and_2_out));
  _18_bit_Register R2 (.in_1(write_data), .Load(clk), .out_4(R2_out_4));  // open: in_3
  // _18_bit_Register R3: pin names not known; wires that end beside it: and_3_out, write_data, clk, and_4_out, R3_p5
  // _18_bit_Register R4: pin names not known; wires that end beside it: write_data, clk, and_5_out, R4_p4
  // _18_bit_Register R5: pin names not known; wires that end beside it: write_data, clk, and_6_out, R5_p4
  // _18_bit_Register R6: pin names not known; wires that end beside it: write_data, clk, and_7_out, R6_p4
  // _18_bit_Register R7: pin names not known; wires that end beside it: write_data, clk, and_8_out, R7_p4
  // _18_bit_Register R8: pin names not known; wires that end beside it: write_data, clk, and_9_out, R8_p4
  // _18_bit_Register R9: pin names not known; wires that end beside it: write_data, clk, and_10_out, R9_p4
  // _18_bit_Register R10: pin names not known; wires that end beside it: write_data, clk, and_11_out, R10_p4
  // _18_bit_Register R11: pin names not known; wires that end beside it: write_data, clk, and_12_out, R11_p4
  // _18_bit_Register R12: pin names not known; wires that end beside it: write_data, clk, and_13_out, R12_p4
  // _18_bit_Register R13: pin names not known; wires that end beside it: write_data, clk, and_14_out, R13_p4
  // _18_bit_Register R14: pin names not known; wires that end beside it: write_data, clk, and_15_out, R14_p4
  // _18_bit_Register R15: pin names not known; wires that end beside it: write_data, clk, and_16_out, and_15_out, R15_p5
  Multiplexer #(.select(4), .width(18), .enable("false")) multiplexer_1 (
    .in0(R0_out_4), .in1(R1_out_4), .in2(R2_out_4), .in3(R3_p5), .in4(R4_p4), .in5(R5_p4), .in6(R6_p4),
    .in7(R7_p4), .in8(R8_p4), .in9(R9_p4), .in10(R10_p4), .in11(R11_p4), .in12(R12_p4), .in13(R13_p4),
    .in14(R14_p4), .in15(R15_p5), .out(Src_Data_1), .sel(Src_Reg_1));
  Multiplexer #(.select(4), .width(18), .enable("false")) multiplexer_2 (
    .in0(R0_out_4), .in1(R1_out_4), .in2(R2_out_4), .in3(R3_p5), .in4(R4_p4), .in5(R5_p4), .in6(R6_p4),
    .in7(R7_p4), .in8(R8_p4), .in9(R9_p4), .in10(R10_p4), .in11(R11_p4), .in12(R12_p4), .in13(R13_p4),
    .in14(R14_p4), .in15(R15_p5), .out(Src_Data_2), .sel(Src_Reg_2));
endmodule

module load (
  input  [3:0] \reg ,
  input  Load_Enable,
  input  [9:0] address
);

  wire [17:0] instruction_unit_1_out_5;

  Register_File register_file_1 (
    .Dest_Reg(\reg ), .write_enable(1'b1), .write_data(instruction_unit_1_out_5), .clk(Load_Enable));  // open: Src_Data_1, Src_Data_2, Src_Reg_1, Src_Reg_2
  instruction_unit instruction_unit_1 (
    .address(address), .out_5(instruction_unit_1_out_5));  // open: Load, Store, dataStored
endmodule

module andGate (
  input  [17:0] regData1,
  input  [17:0] regData2,
  input  _16th_bit,
  input  [17:0] immValue,
  output [17:0] out_5
);

  wire [17:0] multiplexer_1_out;

  Multiplexer #(.width(18), .enable("false")) multiplexer_1 (
    .in0(regData2), .in1(immValue), .out(multiplexer_1_out), .sel(_16th_bit));
  assign out_5 = regData1 & multiplexer_1_out;  // AND_Gate and_1, 18 bits wide
endmodule

module addGate (
  input  [17:0] regData1,
  input  [17:0] regData2,
  input  _16th_bit,
  input  [17:0] immValue,
  output [17:0] out_5
);

  wire [17:0] multiplexer_1_out;

  Multiplexer #(.width(18), .enable("false")) multiplexer_1 (
    .in0(regData2), .in1(immValue), .out(multiplexer_1_out), .sel(_16th_bit));
  _18_bit_Adder u_18_bit_adder_1 (.out_3(out_5), .Reg_1(multiplexer_1_out), .Reg_2(regData1));
endmodule

module norGate (
  input  [17:0] regData1,
  input  [17:0] regData2,
  output [17:0] out_3
);

  wire [17:0] or_1_out;

  assign or_1_out = regData1 | regData2;  // OR_Gate or_1, 18 bits wide
  assign out_3 = ~or_1_out;  // NOT_Gate not_1, 18 bits wide
endmodule

module nandGate (
  input  [17:0] regData1,
  input  [17:0] regData2,
  output [17:0] out_3
);

  wire [17:0] and_1_out;

  assign and_1_out = regData1 & regData2;  // AND_Gate and_1, 18 bits wide
  assign out_3 = ~and_1_out;  // NOT_Gate not_1, 18 bits wide
endmodule

module Program_Counter_PC (
  input  [9:0] in_1,
  input  First_pin,
  input  stopper,
  output [9:0] out_4
);

  wire not_1_out;
  wire [9:0] bit_extender_1_out, multiplexer_1_out, n10_bit_register_1_out_3, n10to1bit_adder_1_out_3;

  Multiplexer #(.width(10), .enable("false")) multiplexer_1 (
    .in0(in_1), .in1(n10_bit_register_1_out_3), .out(multiplexer_1_out), .sel(First_pin));
  _10_bit_Register u_10_bit_register_1 (
    .in_1(n10to1bit_adder_1_out_3), .Load(stopper), .out_3(n10_bit_register_1_out_3));
  not not_1 (not_1_out, stopper);
  _10_bit_Register u_10_bit_register_2 (.in_1(multiplexer_1_out), .Load(not_1_out), .out_3(out_4));
  assign bit_extender_1_out = {{9{1'b0}}, 1'b1};  // Bit_Extender bit_extender_1
  _10to1bit_adder u_10to1bit_adder_1 (.PC(out_4), ._1(bit_extender_1_out), .out_3(n10to1bit_adder_1_out_3));
endmodule

module _10to1bit_adder (
  input  [9:0] _1,
  input  [9:0] PC,
  output [9:0] out_3
);

  wire half_adder_1_cout, half_adder_3_cout, half_adder_4_cout, half_adder_5_cout, half_adder_6_cout,
       half_adder_7_cout, half_adder_8_cout, half_adder_9_cout, half_adder_10_cout;

  Half_Adder half_adder_1 (.in_1(PC[8]), .in_2(half_adder_4_cout), .Cout(half_adder_1_cout), .S(out_3[8]));
  Half_Adder half_adder_2 (.in_1(PC[9]), .in_2(half_adder_1_cout), .S(out_3[9]));  // open: Cout
  Half_Adder half_adder_3 (.in_1(PC[6]), .in_2(half_adder_6_cout), .Cout(half_adder_3_cout), .S(out_3[6]));
  Half_Adder half_adder_4 (.in_1(PC[7]), .in_2(half_adder_3_cout), .Cout(half_adder_4_cout), .S(out_3[7]));
  Half_Adder half_adder_5 (.in_1(PC[4]), .in_2(half_adder_8_cout), .Cout(half_adder_5_cout), .S(out_3[4]));
  Half_Adder half_adder_6 (.in_1(PC[5]), .in_2(half_adder_5_cout), .Cout(half_adder_6_cout), .S(out_3[5]));
  Half_Adder half_adder_7 (.in_1(PC[2]), .in_2(half_adder_10_cout), .Cout(half_adder_7_cout), .S(out_3[2]));
  Half_Adder half_adder_8 (.in_1(PC[3]), .in_2(half_adder_7_cout), .Cout(half_adder_8_cout), .S(out_3[3]));
  Half_Adder half_adder_9 (.in_1(PC[0]), .in_2(_1[0]), .Cout(half_adder_9_cout), .S(out_3[0]));
  Half_Adder half_adder_10 (.in_1(PC[1]), .in_2(half_adder_9_cout), .Cout(half_adder_10_cout), .S(out_3[1]));
endmodule

module _10_bit_adder (
  input  [9:0] PC,
  input  [9:0] PC_2,
  output [9:0] out_3
);

  wire full_adder_1_cout, full_adder_3_cout, full_adder_4_cout, full_adder_5_cout, full_adder_6_cout,
       full_adder_7_cout, full_adder_8_cout, full_adder_9_cout, half_adder_1_cout;

  Full_Adder full_adder_1 (.i0(PC_2[8]), .i1(PC[8]), .Cin(full_adder_4_cout), .Sum(out_3[8]), .Cout(full_adder_1_cout));
  Full_Adder full_adder_2 (.i0(PC_2[9]), .i1(PC[9]), .Cin(full_adder_1_cout), .Sum(out_3[9]));  // open: Cout
  Full_Adder full_adder_3 (.i0(PC_2[6]), .i1(PC[6]), .Cin(full_adder_6_cout), .Sum(out_3[6]), .Cout(full_adder_3_cout));
  Full_Adder full_adder_4 (.i0(PC_2[7]), .i1(PC[7]), .Cin(full_adder_3_cout), .Sum(out_3[7]), .Cout(full_adder_4_cout));
  Full_Adder full_adder_5 (.i0(PC_2[4]), .i1(PC[4]), .Cin(full_adder_8_cout), .Sum(out_3[4]), .Cout(full_adder_5_cout));
  Full_Adder full_adder_6 (.i0(PC_2[5]), .i1(PC[5]), .Cin(full_adder_5_cout), .Sum(out_3[5]), .Cout(full_adder_6_cout));
  Full_Adder full_adder_7 (.i0(PC_2[2]), .i1(PC[2]), .Cin(full_adder_9_cout), .Sum(out_3[2]), .Cout(full_adder_7_cout));
  Full_Adder full_adder_8 (.i0(PC_2[3]), .i1(PC[3]), .Cin(full_adder_7_cout), .Sum(out_3[3]), .Cout(full_adder_8_cout));
  Half_Adder half_adder_1 (.in_1(PC_2[0]), .in_2(PC[0]), .Cout(half_adder_1_cout), .S(out_3[0]));
  Full_Adder full_adder_9 (.i0(PC_2[1]), .i1(PC[1]), .Cin(half_adder_1_cout), .Sum(out_3[1]), .Cout(full_adder_9_cout));
endmodule

module _1_bit_compare (
  input  in_1,
  input  in_2,
  output Same,
  output GreaterFlag
);

  wire half_adder_1_s, xor_1_out;

  xor xor_1 (xor_1_out, in_1, in_2);
  not not_1 (Same, xor_1_out);
  Half_Adder half_adder_1 (.in_1(in_1), .in_2(in_2), .S(half_adder_1_s));  // open: Cout
  and and_1 (GreaterFlag, half_adder_1_s, in_1);
endmodule

module half_cmp (
  input  a,
  input  b,
  output eq,
  output gt,
  output lt
);

  wire xor_1_out;

  xnor xnor_1 (eq, a, b);
  and and_1 (gt, a, xor_1_out);
  xor xor_1 (xor_1_out, a, b);
  and and_2 (lt, xor_1_out, b);
endmodule

module full_cmp (
  input  a,
  input  b,
  input  gt,
  input  lt,
  input  eq,
  output g,
  output lt_2,
  output eq_2
);

  wire and_1_out, and_2_out, xnor_1_out;

  and and_1 (and_1_out, a, ~b, eq);  // AND_Gate
  and and_2 (and_2_out, ~a, b, eq);  // AND_Gate
  xnor xnor_1 (xnor_1_out, a, b);
  or or_1 (g, and_1_out, gt);
  or or_2 (lt_2, and_2_out, lt);
  and and_3 (eq_2, xnor_1_out, eq);
endmodule

module Control_Unit (
  input  [9:0] in_1,
  input  in_2,
  input  in_3,
  output [17:0] FullCode,
  output RegFileWrite,
  output _3_Reg_signal,
  output Jump,
  output MemoryStore,
  output MemoryLoad,
  output ALU_signal,
  output imm_signal
);

  wire ADD, ADDI, AND, ANDI, CMP, JA, JAE, JB, JBE, JE, NAND, NOR;

  Memory_Unit memory_unit_1 (.PC(in_1), .mx_controller(in_2), .counter(in_3), .out_4(FullCode));
  or or_1 (ALU_signal, ADD, AND, NAND, NOR, ADDI, ANDI);
  or or_2 (imm_signal, ANDI, ADDI);
  Decoder #(.select(4), .enable("false")) decoder_1 (
    .out0(ADD), .out1(AND), .out2(NAND), .out3(NOR), .out4(ADDI), .out5(ANDI), .out6(MemoryLoad),
    .out7(MemoryStore), .out8(CMP), .out9(Jump), .out10(JA), .out11(JE), .out12(JB), .out13(JAE),
    .out14(JBE), .out15(JBE), .sel(FullCode[17:14]));
  or or_3 (_3_Reg_signal, ADD, AND, NOR, NAND);
  or Art (RegFileWrite, NOR, AND, NOR, ADD, MemoryStore, MemoryLoad, ANDI, ADDI);

  // Other names for the same wires on the sheet: Opcode[3:0] = FullCode[17:14]; LD = MemoryLoad; ST = MemoryStore
endmodule

module Memory_Unit (
  input  [9:0] PC,
  input  counter,
  input  mx_controller,
  output [17:0] out_4
);

  wire [9:0] program_counter_pc_1_out_4;

  Program_Counter_PC program_counter_pc_1 (
    .in_1(PC), .First_pin(mx_controller), .stopper(counter), .out_4(program_counter_pc_1_out_4));
  ROM #(.addrWidth(10), .dataWidth(18)) rom_1 (.addr(program_counter_pc_1_out_4), .data(out_4));  // open: sel

  // Notes on the sheet:
  //   contents of rom_1 (hex, n*v repeats v):
  //   1408 10c4c 1940c 1d9c8 21c08 28064 2c065 3006e 3406f 383e8 24003 66ac f378 2fc14 14653
endmodule

module instruction_unit (
  input  [9:0] address,
  input  [17:0] dataStored,
  input  Store,
  input  Load,
  output [17:0] out_5
);

  RAM #(.addrWidth(10), .dataWidth(18), .bus("separate")) ram_1 (
    .addr(address), .din(dataStored), .data(out_5), .str(Store), .sel(1'b1), .ld(Load), .clr(1'b0));  // open: clk
endmodule

module JPCond (
  input  [17:0] in_1,
  input  [17:0] in_2,
  output JE,
  output JA,
  output JB
);

  CMP_Unit cmp_unit_1 (.in_1(in_1), .in_2(in_2), .eq(JE), .gt(JA), .lt(JB));
endmodule
